# Fritzing sketch SPI Arduino Slave (saved by Fritzing 0.9.3b)
breadboards: 1

parts:
  Part1 = Arduino Uno (Rev3)
  U1 = STM32F103C8T6 blue mini board  # not connected
  U2 = 7-SEGMENT-4DIGIT [package=7-segment-4digit_longpads_for_pogobed]

nets:
  N1: Part1.D8, U2.1
  N2: Part1.GND, U2.8
  N3: Part1.D2, U2.9
  N4: Part1.D3_PWM, U2.11
  N5: Part1.D4, U2.13
  N6: Part1.D5_PWM, U2.14
  N7: Part1.D6_PWM, U2.15
  N8: Part1.D7, U2.16
  N9: Part1.5V, U2.7

notes:
  blue - A, red - B, black - C, yellow - D, green - E,grey - F, white - G, orange is Cathode and brown is common  gnd
  cyan -SCLK, brown-MISO, purple-MOSI, pink-SS
